# Fritzing sketch xiao-ble-wiring (saved by Fritzing 0.9.4)

parts:
  A1 = XIAO NRF52840 sense SMD
  Mod1 = OLED Mono 0.56 inch blue or white
  S1 = Momentary Switch [package=ksa_sealed_tac_switch]
  A2 = XIAO NRF52840 sense SMD
  Mod2 = OLED Mono 0.56 inch blue or white
  S2 = Momentary Switch [package=ksa_sealed_tac_switch]

nets:
  N1: A1.Pin_2, A1.Pin_13, A1.Pin_21, Mod1.GND
  N2: A1.Pin_7, S1.1
  N3: A1.Pin_9, Mod1.SDA
  N4: A1.Pin_10, Mod1.SCL
  N5: A1.Pin_20, Mod1.VCC
  N6: A2.Pin_2, A2.Pin_13, A2.Pin_21, Mod2.GND
  N7: A2.Pin_7, S2.1
  N8: A2.Pin_9, Mod2.SDA
  N9: A2.Pin_10, Mod2.SCL
  N10: A2.Pin_20, Mod2.VCC

notes:
  5v power source
  Screen power 3.3v

custom parts:
  XIAO NRF52840 sense SMD: The Seeed Studio XIAO family, Seeed Studio XIAO nRF52840 is equipped with a powerful Nordic nRF52840 MCU which integrates Bluetooth 5.0 connectivity. This is the SMD version there is also a THT version of the part.
  OLED Mono 0.56 inch blue or white: OLED, I2C 3.3V - 5V Blue and White text versions
